# Fritzing sketch Untitled Sketch (saved by Fritzing 0.9.3b)

parts:
  U1 = NodeMCU V1.0
  U2 = NodeMCU V1.0

nets:
  N1: U1.RX, U2.TX
  N2: U1.TX, U2.RX
  GND: U1.GND, U2.GND
  3V3: U1.3V3, U2.3V3

notes:
  HOST
  CLIENT

custom parts:
  NodeMCU V1.0: ESP8266 based NodeMCU
